// Digital circuit CTRLUNIT.dig as structural Verilog
module CTRLUNIT (
  input  [7:0] OPC,
  input  [2:0] microstep,
  input  Z,
  input  C,
  input  N,
  input  V,
  input  I,
  output [15:0] C0_15,
  output [15:0] C16_31,
  output [15:0] C32_47
);

  ROM #(.AddrBits(16), .Bits(16)) _1ROM (.A({I, V, N, C, Z, microstep, OPC}), .sel(1'b1), .D(C0_15));
  ROM #(.AddrBits(16), .Bits(16)) _2ROM (.A({I, V, N, C, Z, microstep, OPC}), .sel(1'b1), .D(C16_31));
  ROM #(.AddrBits(16), .Bits(16)) _3ROM (.A({I, V, N, C, Z, microstep, OPC}), .sel(1'b1), .D(C32_47));

  // Notes on the sheet:
  //   contents of _1ROM (hex, n*v repeats v):
  //   256*77da,8*f1bb,8*f1fb,61bb,51bb,6*73fb,61fb,61fb,6*73fb,8*f47f
  //   ,8*b5ff,8*f5ff,8*787f,8*39ff,16*79ff,8*f5ff,8*f1fb,8*f1bb,32*f1fb
  //   ,8*f1bb,16*f1fb,16*f1bb,16*f1fb,8*71fb,8*71bb,31fd,71fb,5*73fb
  //   ,31fd,7*73fb,71fd,71fb,71fb,7bef,7bef,4*73fb,31ff,63fb,71ff,71fb,71fb
  //   ,73fb,f1fb,f1fb,7bef,79ff,75ff,73ff,77ff,71fb,71fb,73fb,234*73fa
  //   ,7bf6,7bf6,5*73fa,51fa,6*73fa,7bf6,73fa,73fa,67fe,67fe,237*73fa
  //   ,31fc,71fc,12*73fa,73ff,73fa,73fa,57fe,57fe,251*73fa,77de,73fa,73fa
  //   ,31fc,31fc,251*73fa,63ba,255*73fa,77de,255*73fa,51ba,7*73fa,256*77da
  //   ,8*f1bb,8*f1fb,61bb,51bb,6*73fb,61fb,61fb,6*73fb,8*f47f,8*b5ff
  //   ,8*f5ff,8*787f,8*39ff,16*79ff,8*f5ff,8*f1fb,8*f1bb,32*f1fb,8*f1bb
  //   ,16*f1fb,16*f1bb,16*f1fb,8*71fb,8*71bb,31fd,71fb,5*73fb,31fd,7*73fb
  //   ,71fd,71fb,71fb,7bef,7bef,4*73fb,31ff,63fb,71ff,71fb,71fb,73fb
  //   ,f1fb,f1fb,7bef,79ff,75ff,73ff,77ff,71fb,71fb,73fb,234*73fa,7bf6,7bf6
  //   ,5*73fa,51fa,6*73fa,7bf6,73fa,73fa,67fe,67fe,237*73fa,31fc,71fc
  //   ,12*73fa,73ff,73fa,73fa,57fe,57fe,251*73fa,77de,73fa,73fa,31fc,31fc
  //   ,251*73fa,63ba,255*73fa,77de,255*73fa,51ba,7*73fa,256*77da,8*f1bb
  //   ,8*f1fb,61bb,51bb,6*73fb,61fb,61fb,6*73fb,8*f47f,8*b5ff,8*f5ff
  //   ,8*787f,8*39ff,16*79ff,8*f5ff,8*f1fb,8*f1bb,32*f1fb,8*f1bb,16*f1fb
  //   ,16*f1bb,16*f1fb,8*71fb,8*71bb,31fd,71fb,5*73fb,31fd,7*73fb,71fd
  //   ,71fb,71fb,7bef,7bef,4*73fb,31ff,63fb,71ff,71fb,71fb,73fb,f1fb,f1fb
  //   ,7bef,79ff,75ff,73ff,77ff,71fb,71fb,73fb,234*73fa,7bf6,7bf6,5*73fa
  //   ,51fa,6*73fa,7bf6,73fa,73fa,67fe,67fe,237*73fa,31fc,71fc,12*73fa
  //   ,73ff,73fa,73fa,57fe,57fe,251*73fa,77de,73fa,73fa,31fc,31fc,251*73fa
  //   ,63ba,255*73fa,77de,255*73fa,51ba,7*73fa,256*77da,8*f1bb,8*f1fb
  //   ,61bb,51bb,6*73fb,61fb,61fb,6*73fb,8*f47f,8*b5ff,8*f5ff,8*787f
  //   ,8*39ff,16*79ff,8*f5ff,8*f1fb,8*f1bb,32*f1fb,8*f1bb,16*f1fb,16*f1bb
  //   ,16*f1fb,8*71fb,8*71bb,31fd,71fb,5*73fb,31fd,7*73fb,71fd,71fb,71fb
  //   ,7bef,7bef,4*73fb,31ff,63fb,71ff,71fb,71fb,73fb,f1fb,f1fb,7bef
  //   ,79ff,75ff,73ff,77ff,71fb,71fb,73fb,234*73fa,7bf6,7bf6,5*73fa
  //   ,51fa,6*73fa,7bf6,73fa,73fa,67fe,67fe,237*73fa,31fc,71fc,12*73fa
  //   ,73ff,73fa,73fa,57fe,57fe,251*73fa,77de,73fa,73fa,31fc,31fc,251*73fa
  //   ,63ba,255*73fa,77de,255*73fa,51ba,7*73fa,256*77da,8*f1bb,8*f1fb
  //   ,61bb,51bb,6*73fb,61fb,61fb,6*73fb,8*f47f,8*b5ff,8*f5ff,8*787f
  //   ,8*39ff,16*79ff,8*f5ff,8*f1fb,8*f1bb,32*f1fb,8*f1bb,16*f1fb,16*f1bb
  //   ,16*f1fb,8*71fb,8*71bb,31fd,71fb,5*73fb,31fd,7*73fb,71fd,71fb,71fb
  //   ,7bef,7bef,4*73fb,31ff,63fb,71ff,71fb,71fb,73fb,f1fb,f1fb,7bef
  //   ,79ff,75ff,73ff,77ff,71fb,71fb,73fb,234*73fa,7bf6,7bf6,5*73fa
  //   ,51fa,6*73fa,7bf6,73fa,73fa,67fe,67fe,237*73fa,31fc,71fc,12*73fa
  //   ,73ff,73fa,73fa,57fe,57fe,251*73fa,77de,73fa,73fa,31fc,31fc,251*73fa
  //   ,63ba,255*73fa,77de,255*73fa,51ba,7*73fa,256*77da,8*f1bb,8*f1fb
  //   ,61bb,51bb,6*73fb,61fb,61fb,6*73fb,8*f47f,8*b5ff,8*f5ff,8*787f
  //   ,8*39ff,16*79ff,8*f5ff,8*f1fb,8*f1bb,32*f1fb,8*f1bb,16*f1fb,16*f1bb
  //   ,16*f1fb,8*71fb,8*71bb,31fd,71fb,5*73fb,31fd,7*73fb,71fd,71fb,71fb
  //   ,7bef,7bef,4*73fb,31ff,63fb,71ff,71fb,71fb,73fb,f1fb,f1fb,7bef
  //   ,79ff,75ff,73ff,77ff,71fb,71fb,73fb,234*73fa,7bf6,7bf6,5*73fa
  //   ,51fa,6*73fa,7bf6,73fa,73fa,67fe,67fe,237*73fa,31fc,71fc,12*73fa
  //   ,73ff,73fa,73fa,57fe,57fe,251*73fa,77de,73fa,73fa,31fc,31fc,251*73fa
  //   ,63ba,255*73fa,77de,255*73fa,51ba,7*73fa,256*77da,8*f1bb,8*f1fb
  //   ,61bb,51bb,6*73fb,61fb,61fb,6*73fb,8*f47f,8*b5ff,8*f5ff,8*787f
  //   ,8*39ff,16*79ff,8*f5ff,8*f1fb,8*f1bb,32*f1fb,8*f1bb,16*f1fb,16*f1bb
  //   ,16*f1fb,8*71fb,8*71bb,31fd,71fb,5*73fb,31fd,7*73fb,71fd,71fb,71fb
  //   ,7bef,7bef,4*73fb,31ff,63fb,71ff,71fb,71fb,73fb,f1fb,f1fb,7bef
  //   ,79ff,75ff,73ff,77ff,71fb,71fb,73fb,234*73fa,7bf6,7bf6,5*73fa
  //   ,51fa,6*73fa,7bf6,73fa,73fa,67fe,67fe,237*73fa,31fc,71fc,12*73fa
  //   ,73ff,73fa,73fa,57fe,57fe,251*73fa,77de,73fa,73fa,31fc,31fc,251*73fa
  //   ,63ba,255*73fa,77de,255*73fa,51ba,7*73fa,256*77da,8*f1bb,8*f1fb
  //   ,61bb,51bb,6*73fb,61fb,61fb,6*73fb,8*f47f,8*b5ff,8*f5ff,8*787f
  //   ,8*39ff,16*79ff,8*f5ff,8*f1fb,8*f1bb,32*f1fb,8*f1bb,16*f1fb,16*f1bb
  //   ,16*f1fb,8*71fb,8*71bb,31fd,71fb,5*73fb,31fd,7*73fb,71fd,71fb,71fb
  //   ,7bef,7bef,4*73fb,31ff,63fb,71ff,71fb,71fb,73fb,f1fb,f1fb,7bef
  //   ,79ff,75ff,73ff,77ff,71fb,71fb,73fb,234*73fa,7bf6,7bf6,5*73fa
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  //   contents of _2ROM (hex, n*v repeats v):
  //   264*350a,8*350b,8*350a,350b,350b,22*350a,8*3502,16*350b,8*3503
  //   ,8*350b,8*350a,8*157b,8*157a,8*177b,8*175b,8*155b,8*15db,8*15da
  //   ,8*15bb,8*159b,8*177a,8*155a,16*310a,8*174b,8*174a,15*350a,3502
  //   ,3508,350c,8*350a,3502,6*350a,250a,150a,350a,550a,494*350a,3502
  //   ,12*350a,250a,1295*350a,8*350b,8*350a,350b,350b,22*350a,8*3502
  //   ,16*350b,8*3503,8*350b,8*350a,8*157b,8*157a,8*177b,8*175b,8*155b
  //   ,8*15db,8*15da,8*15bb,8*159b,8*177a,8*155a,16*310a,8*174b,8*174a
  //   ,15*350a,3502,3508,350c,8*350a,3502,6*350a,250a,150a,350a,550a
  //   ,494*350a,3502,12*350a,250a,1295*350a,8*350b,8*350a,350b,350b
  //   ,22*350a,8*3502,16*350b,8*3503,8*350b,8*350a,8*157b,8*157a,8*177b
  //   ,8*175b,8*155b,8*15db,8*15da,8*15bb,8*159b,8*177a,8*155a,16*310a
  //   ,8*174b,8*174a,15*350a,3502,3508,350c,8*350a,3502,6*350a,250a
  //   ,150a,350a,550a,494*350a,3502,12*350a,250a,1295*350a,8*350b,8*350a
  //   ,350b,350b,22*350a,8*3502,16*350b,8*3503,8*350b,8*350a,8*157b
  //   ,8*157a,8*177b,8*175b,8*155b,8*15db,8*15da,8*15bb,8*159b,8*177a
  //   ,8*155a,16*310a,8*174b,8*174a,15*350a,3502,3508,350c,8*350a,3502
  //   ,6*350a,250a,150a,350a,550a,494*350a,3502,12*350a,250a,1295*350a
  //   ,8*350b,8*350a,350b,350b,22*350a,8*3502,16*350b,8*3503,8*350b
  //   ,8*350a,8*157b,8*157a,8*177b,8*175b,8*155b,8*15db,8*15da,8*15bb
  //   ,8*159b,8*177a,8*155a,16*310a,8*174b,8*174a,15*350a,3502,3508
  //   ,350c,8*350a,3502,6*350a,250a,150a,350a,550a,494*350a,3502,12*350a
  //   ,250a,1295*350a,8*350b,8*350a,350b,350b,22*350a,8*3502,16*350b
  //   ,8*3503,8*350b,8*350a,8*157b,8*157a,8*177b,8*175b,8*155b,8*15db
  //   ,8*15da,8*15bb,8*159b,8*177a,8*155a,16*310a,8*174b,8*174a,15*350a
  //   ,3502,3508,350c,8*350a,3502,6*350a,250a,150a,350a,550a,494*350a
  //   ,3502,12*350a,250a,1295*350a,8*350b,8*350a,350b,350b,22*350a,8*3502
  //   ,16*350b,8*3503,8*350b,8*350a,8*157b,8*157a,8*177b,8*175b,8*155b
  //   ,8*15db,8*15da,8*15bb,8*159b,8*177a,8*155a,16*310a,8*174b,8*174a
  //   ,15*350a,3502,3508,350c,8*350a,3502,6*350a,250a,150a,350a,550a
  //   ,494*350a,3502,12*350a,250a,1295*350a,8*350b,8*350a,350b,350b
  //   ,22*350a,8*3502,16*350b,8*3503,8*350b,8*350a,8*157b,8*157a,8*177b
  //   ,8*175b,8*155b,8*15db,8*15da,8*15bb,8*159b,8*177a,8*155a,16*310a
  //   ,8*174b,8*174a,15*350a,3502,3508,350c,8*350a,3502,6*350a,250a
  //   ,150a,350a,550a,494*350a,3502,12*350a,250a,1295*350a,8*350b,8*350a
  //   ,350b,350b,22*350a,8*3502,16*350b,8*3503,8*350b,8*350a,8*157b
  //   ,8*157a,8*177b,8*175b,8*155b,8*15db,8*15da,8*15bb,8*159b,8*177a
  //   ,8*155a,16*310a,8*174b,8*174a,15*350a,3502,3508,350c,8*350a,3502
  //   ,6*350a,250a,150a,350a,550a,494*350a,3502,12*350a,250a,1295*350a
  //   ,8*350b,8*350a,350b,350b,22*350a,8*3502,16*350b,8*3503,8*350b
  //   ,8*350a,8*157b,8*157a,8*177b,8*175b,8*155b,8*15db,8*15da,8*15bb
  //   ,8*159b,8*177a,8*155a,16*310a,8*174b,8*174a,15*350a,3502,3508
  //   ,350c,8*350a,3502,6*350a,250a,150a,350a,550a,494*350a,3502,12*350a
  //   ,250a,1295*350a,8*350b,8*350a,350b,350b,22*350a,8*3502,16*350b
  //   ,8*3503,8*350b,8*350a,8*157b,8*157a,8*177b,8*175b,8*155b,8*15db
  //   ,8*15da,8*15bb,8*159b,8*177a,8*155a,16*310a,8*174b,8*174a,15*350a
  //   ,3502,3508,350c,8*350a,3502,6*350a,250a,150a,350a,550a,494*350a
  //   ,3502,12*350a,250a,1295*350a,8*350b,8*350a,350b,350b,22*350a,8*3502
  //   ,16*350b,8*3503,8*350b,8*350a,8*157b,8*157a,8*177b,8*175b,8*155b
  //   ,8*15db,8*15da,8*15bb,8*159b,8*177a,8*155a,16*310a,8*174b,8*174a
  //   ,15*350a,3502,3508,350c,8*350a,3502,6*350a,250a,150a,350a,550a
  //   ,494*350a,3502,12*350a,250a,1295*350a,8*350b,8*350a,350b,350b
  //   ,22*350a,8*3502,16*350b,8*3503,8*350b,8*350a,8*157b,8*157a,8*177b
  //   ,8*175b,8*155b,8*15db,8*15da,8*15bb,8*159b,8*177a,8*155a,16*310a
  //   ,8*174b,8*174a,15*350a,3502,3508,350c,8*350a,3502,6*350a,250a
  //   ,150a,350a,550a,494*350a,3502,12*350a,250a,1295*350a,8*350b,8*350a
  //   ,350b,350b,22*350a,8*3502,16*350b,8*3503,8*350b,8*350a,8*157b
  //   ,8*157a,8*177b,8*175b,8*155b,8*15db,8*15da,8*15bb,8*159b,8*177a
  //   ,8*155a,16*310a,8*174b,8*174a,15*350a,3502,3508,350c,8*350a,3502
  //   ,6*350a,250a,150a,350a,550a,494*350a,3502,12*350a,250a,1295*350a
  //   ,8*350b,8*350a,350b,350b,22*350a,8*3502,16*350b,8*3503,8*350b
  //   ,8*350a,8*157b,8*157a,8*177b,8*175b,8*155b,8*15db,8*15da,8*15bb
  //   ,8*159b,8*177a,8*155a,16*310a,8*174b,8*174a,15*350a,3502,3508
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  //   contents of _3ROM (hex, n*v repeats v):
  //   336*3f4,8*3d8,8*3d0,138*3f4,3d8,3d8,4*3f4,3e4,3b4,3e4,3f0,3f8
  //   ,3f4,374,3b4,3d8,3d8,3d0,3d0,3d2,3f7,3f6,235*3f4,3d8,3d8,5*3f4
  //   ,374,6*3f4,3d8,3f4,3f4,3d0,3d0,251*3f4,3d8,3f4,3f4,3d4,3d0,251*3f4
  //   ,1f4,511*3f4,5f4,599*3f4,8*3d8,8*3d0,138*3f4,3d8,3d8,4*3f4,3e4
  //   ,3b4,3e4,3f0,3f8,3f4,374,3b4,3d8,3d8,3d0,3d0,3d2,3f7,3f6,235*3f4
  //   ,3d8,3d8,5*3f4,374,6*3f4,3d8,3f4,3f4,3d0,3d0,251*3f4,3d8,3f4,3f4
  //   ,3d4,3d0,251*3f4,1f4,511*3f4,5f4,599*3f4,8*3d8,8*3d0,138*3f4,3d8,3d8
  //   ,4*3f4,3e4,3b4,3e4,3f0,3f8,3f4,374,3b4,3d8,3d8,3d0,3d0,3d2,3f7
  //   ,3f6,235*3f4,3d8,3d8,5*3f4,374,6*3f4,3d8,3f4,3f4,3d0,3d0,251*3f4
  //   ,3d8,3f4,3f4,3d4,3d0,251*3f4,1f4,511*3f4,5f4,599*3f4,8*3d8,8*3d0
  //   ,138*3f4,3d8,3d8,4*3f4,3e4,3b4,3e4,3f0,3f8,3f4,374,3b4,3d8,3d8
  //   ,3d0,3d0,3d2,3f7,3f6,235*3f4,3d8,3d8,5*3f4,374,6*3f4,3d8,3f4,3f4
  //   ,3d0,3d0,251*3f4,3d8,3f4,3f4,3d4,3d0,251*3f4,1f4,511*3f4,5f4,599*3f4
  //   ,8*3d8,8*3d0,138*3f4,3d8,3d8,4*3f4,3e4,3b4,3e4,3f0,3f8,3f4,374
  //   ,3b4,3d8,3d8,3d0,3d0,3d2,3f7,3f6,235*3f4,3d8,3d8,5*3f4,374,6*3f4
  //   ,3d8,3f4,3f4,3d0,3d0,251*3f4,3d8,3f4,3f4,3d4,3d0,251*3f4,1f4,511*3f4
  //   ,5f4,599*3f4,8*3d8,8*3d0,138*3f4,3d8,3d8,4*3f4,3e4,3b4,3e4,3f0
  //   ,3f8,3f4,374,3b4,3d8,3d8,3d0,3d0,3d2,3f7,3f6,235*3f4,3d8,3d8,5*3f4
  //   ,374,6*3f4,3d8,3f4,3f4,3d0,3d0,251*3f4,3d8,3f4,3f4,3d4,3d0,251*3f4
  //   ,1f4,511*3f4,5f4,599*3f4,8*3d8,8*3d0,138*3f4,3d8,3d8,4*3f4,3e4
  //   ,3b4,3e4,3f0,3f8,3f4,374,3b4,3d8,3d8,3d0,3d0,3d2,3f7,3f6,235*3f4
  //   ,3d8,3d8,5*3f4,374,6*3f4,3d8,3f4,3f4,3d0,3d0,251*3f4,3d8,3f4,3f4
  //   ,3d4,3d0,251*3f4,1f4,511*3f4,5f4,599*3f4,8*3d8,8*3d0,138*3f4,3d8,3d8
  //   ,4*3f4,3e4,3b4,3e4,3f0,3f8,3f4,374,3b4,3d8,3d8,3d0,3d0,3d2,3f7
  //   ,3f6,235*3f4,3d8,3d8,5*3f4,374,6*3f4,3d8,3f4,3f4,3d0,3d0,251*3f4
  //   ,3d8,3f4,3f4,3d4,3d0,251*3f4,1f4,511*3f4,5f4,599*3f4,8*3d8,8*3d0
  //   ,138*3f4,3d8,3d8,4*3f4,3e4,3b4,3e4,3f0,3f8,3f4,374,3b4,3d8,3d8
  //   ,3d0,3d0,3d2,3f7,3f6,235*3f4,3d8,3d8,5*3f4,374,6*3f4,3d8,3f4,3f4
  //   ,3d0,3d0,251*3f4,3d8,3f4,3f4,3d4,3d0,251*3f4,1f4,511*3f4,5f4,599*3f4
  //   ,8*3d8,8*3d0,138*3f4,3d8,3d8,4*3f4,3e4,3b4,3e4,3f0,3f8,3f4,374
  //   ,3b4,3d8,3d8,3d0,3d0,3d2,3f7,3f6,235*3f4,3d8,3d8,5*3f4,374,6*3f4
  //   ,3d8,3f4,3f4,3d0,3d0,251*3f4,3d8,3f4,3f4,3d4,3d0,251*3f4,1f4,511*3f4
  //   ,5f4,599*3f4,8*3d8,8*3d0,138*3f4,3d8,3d8,4*3f4,3e4,3b4,3e4,3f0
  //   ,3f8,3f4,374,3b4,3d8,3d8,3d0,3d0,3d2,3f7,3f6,235*3f4,3d8,3d8,5*3f4
  //   ,374,6*3f4,3d8,3f4,3f4,3d0,3d0,251*3f4,3d8,3f4,3f4,3d4,3d0,251*3f4
  //   ,1f4,511*3f4,5f4,599*3f4,8*3d8,8*3d0,138*3f4,3d8,3d8,4*3f4,3e4
  //   ,3b4,3e4,3f0,3f8,3f4,374,3b4,3d8,3d8,3d0,3d0,3d2,3f7,3f6,235*3f4
  //   ,3d8,3d8,5*3f4,374,6*3f4,3d8,3f4,3f4,3d0,3d0,251*3f4,3d8,3f4,3f4
  //   ,3d4,3d0,251*3f4,1f4,511*3f4,5f4,599*3f4,8*3d8,8*3d0,138*3f4,3d8,3d8
  //   ,4*3f4,3e4,3b4,3e4,3f0,3f8,3f4,374,3b4,3d8,3d8,3d0,3d0,3d2,3f7
  //   ,3f6,235*3f4,3d8,3d8,5*3f4,374,6*3f4,3d8,3f4,3f4,3d0,3d0,251*3f4
  //   ,3d8,3f4,3f4,3d4,3d0,251*3f4,1f4,511*3f4,5f4,599*3f4,8*3d8,8*3d0
  //   ,138*3f4,3d8,3d8,4*3f4,3e4,3b4,3e4,3f0,3f8,3f4,374,3b4,3d8,3d8
  //   ,3d0,3d0,3d2,3f7,3f6,235*3f4,3d8,3d8,5*3f4,374,6*3f4,3d8,3f4,3f4
  //   ,3d0,3d0,251*3f4,3d8,3f4,3f4,3d4,3d0,251*3f4,1f4,511*3f4,5f4,599*3f4
  //   ,8*3d8,8*3d0,138*3f4,3d8,3d8,4*3f4,3e4,3b4,3e4,3f0,3f8,3f4,374
  //   ,3b4,3d8,3d8,3d0,3d0,3d2,3f7,3f6,235*3f4,3d8,3d8,5*3f4,374,6*3f4
  //   ,3d8,3f4,3f4,3d0,3d0,251*3f4,3d8,3f4,3f4,3d4,3d0,251*3f4,1f4,511*3f4
  //   ,5f4,599*3f4,8*3d8,8*3d0,138*3f4,3d8,3d8,4*3f4,3e4,3b4,3e4,3f0
  //   ,3f8,3f4,374,3b4,3d8,3d8,3d0,3d0,3d2,3f7,3f6,235*3f4,3d8,3d8,5*3f4
  //   ,374,6*3f4,3d8,3f4,3f4,3d0,3d0,251*3f4,3d8,3f4,3f4,3d4,3d0,251*3f4
  //   ,1f4,511*3f4,5f4,263*3f4,768*3d8,256*1f4,256*3f4,256*5f4,256*3f4
  //   ,256*2f7,768*3d8,256*1f4,256*3f4,256*5f4,256*3f4,256*2f7,768*3d8
  //   ,256*1f4,256*3f4,256*5f4,256*3f4,256*2f7,768*3d8,256*1f4,256*3f4
  //   ,256*5f4,256*3f4,256*2f7,768*3d8,256*1f4,256*3f4,256*5f4,256*3f4
  //   ,256*2f7,768*3d8,256*1f4,256*3f4,256*5f4,256*3f4,256*2f7,768*3d8
  //   ,256*1f4,256*3f4,256*5f4,256*3f4,256*2f7,768*3d8,256*1f4,256*3f4
  //   ,256*5f4,256*3f4,256*2f7,768*3d8,256*1f4,256*3f4,256*5f4,256*3f4
  //   ,256*2f7,768*3d8,256*1f4,256*3f4,256*5f4,256*3f4,256*2f7,768*3d8
  //   ,256*1f4,256*3f4,256*5f4,256*3f4,256*2f7,768*3d8,256*1f4,256*3f4
  //   ,256*5f4,256*3f4,256*2f7,768*3d8,256*1f4,256*3f4,256*5f4,256*3f4
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endmodule
