// Digital circuit MAR.dig as structural Verilog
module MAR (
  input  [7:0] D_BUS,
  input  nMAR_OE,
  input  nMARL_LD,
  input  nMARH_LD,
  input  RST,
  input  CLK,
  output [15:0] A_BUS
);

  wire MAR_OE, MARH_LD, MARL_LD;

  _74173 _74173_1 (
    .pin1(MAR_OE), .pin2(MAR_OE), .pin3(A_BUS[15]), .pin4(A_BUS[14]), .pin5(A_BUS[13]), .pin6(A_BUS[12]),
    .pin7(CLK), .pin8(1'b0), .pin9(MARH_LD), .pin10(MARH_LD), .pin11(D_BUS[4]), .pin12(D_BUS[5]),
    .pin13(D_BUS[6]), .pin14(D_BUS[7]), .pin15(RST), .pin16(1'b1));
  not not_1 (MAR_OE, nMAR_OE);
  not not_2 (MARL_LD, nMARL_LD);
  not not_3 (MARH_LD, nMARH_LD);
  _74173 _74173_2 (
    .pin1(MAR_OE), .pin2(MAR_OE), .pin3(A_BUS[11]), .pin4(A_BUS[10]), .pin5(A_BUS[9]), .pin6(A_BUS[8]),
    .pin7(CLK), .pin8(1'b0), .pin9(MARH_LD), .pin10(MARH_LD), .pin11(D_BUS[0]), .pin12(D_BUS[1]),
    .pin13(D_BUS[2]), .pin14(D_BUS[3]), .pin15(RST), .pin16(1'b1));
  _74173 _74173_3 (
    .pin1(MAR_OE), .pin2(MAR_OE), .pin3(A_BUS[7]), .pin4(A_BUS[6]), .pin5(A_BUS[5]), .pin6(A_BUS[4]),
    .pin7(CLK), .pin8(1'b0), .pin9(MARL_LD), .pin10(MARL_LD), .pin11(D_BUS[4]), .pin12(D_BUS[5]),
    .pin13(D_BUS[6]), .pin14(D_BUS[7]), .pin15(RST), .pin16(1'b1));
  _74173 _74173_4 (
    .pin1(MAR_OE), .pin2(MAR_OE), .pin3(A_BUS[3]), .pin4(A_BUS[2]), .pin5(A_BUS[1]), .pin6(A_BUS[0]),
    .pin7(CLK), .pin8(1'b0), .pin9(MARL_LD), .pin10(MARL_LD), .pin11(D_BUS[0]), .pin12(D_BUS[1]),
    .pin13(D_BUS[2]), .pin14(D_BUS[3]), .pin15(RST), .pin16(1'b1));
endmodule
